# Fritzing sketch Raspy-Makey (saved by Fritzing 0.9.3b)
circuit board: 12.8742cm x 10.1409cm
breadboards: 1

parts:
  Part1 = MPR121 Breakout
  Pad1 = Pad [width=7.902222222222222 height=9.0311111111111106 connect=center]
  Pad2 = Pad [width=7.902222222222222 height=9.0311111111111106 connect=center]
  Pad3 = Pad [width=7.902222222222222 height=9.0311111111111106 connect=center]
  Pad4 = Pad [width=7.902222222222222 height=9.0311111111111106 connect=center]
  Pad5 = Pad [width=7.902222222222222 height=9.0311111111111106 connect=center]
  Pad6 = Pad [width=7.902222222222222 height=9.0311111111111106 connect=center]
  Pad7 = Pad [width=7.902222222222222 height=9.0311111111111106 connect=center]
  Pad8 = Pad [width=7.902222222222222 height=9.0311111111111106 connect=center]
  Pad9 = Pad [width=7.902222222222222 height=9.0311111111111106 connect=center]
  Pad10 = Pad [width=7.902222222222222 height=9.0311111111111106 connect=center]
  Pad11 = Pad [width=7.902222222222222 height=9.0311111111111106 connect=center]
  Pad12 = Pad [width=7.902222222222222 height=9.0311111111111106 connect=center]
  Pico_H1 = Raspberry Pi Pico H

nets:
  N1: Part1.SCL, Pico_H1.GP9
  N2: Part1.SDA, Pico_H1.GP8
  N3: Part1.ELE11, Pad12.pad
  N4: Part1.ELE10, Pad11.pad
  N5: Part1.ELE9, Pad10.pad
  N6: Part1.ELE8, Pad9.pad
  N7: Part1.ELE7, Pad6.pad
  N8: Part1.ELE6, Pad5.pad
  N9: Part1.ELE5, Pad4.pad
  N10: Part1.ELE4, Pad3.pad
  N11: Part1.ELE3, Pad2.pad
  N12: Part1.ELE2, Pad1.pad
  N13: Part1.ELE1, Pad8.pad
  N14: Part1.ELE0, Pad7.pad
  3.3V: Part1.3.3V, Pico_H1.3V3
  GND: Part1.GND, Pico_H1.GND

notes:
  Raspy Makey
  Raspberry Pi Pico
  MPR121

custom parts:
  Raspberry Pi Pico H: Raspberry Pi Pico H. Based around the RP2040 microcontroller the Pico H is a low cost microcontroller device bringing Raspberry Pi quality, cost, and easy of use to the microcontroller space.

// code stored in the sketch: piano de cola.ino
import time
import board
import busio
import usb_midi
import adafruit_mpr121

# Initializing I2C interface
i2c = busio.I2C(board.GP9, board.GP8)

# Initialize MPR121 for touch sensing
mpr121 = adafruit_mpr121.MPR121(i2c)

# Defining MIDI message types
NOTE_ON = 0x90
NOTE_OFF = 0x80

# Defining MIDI message parameters
MIDI_CHANNEL = 0
MIDI_PORT = usb_midi.ports[0]

# Defining MIDI note mappings for each touch pad
note_mappings = {
    0: 60,
    1: 62,
    2: 64,
    3: 65,
    4: 67,
    5: 69,
    6: 71,
    7: 72,
    8: 74,
    9: 76,
    10: 77,
    11: 79,
}

# Loop to read touch data and send MIDI messages
while True:
    touch_data = mpr121.touched_pins
    for i in range(12):
        if touch_data & (1 << i):
            # Note on message
            midi_msg = [NOTE_ON | MIDI_CHANNEL, note_mappings[i], 127]
            MIDI_PORT.send_message(midi_msg)
        else:
            # Note off message
            midi_msg = [NOTE_OFF | MIDI_CHANNEL, note_mappings[i], 0]
            MIDI_PORT.send_message(midi_msg)
    time.sleep(0.01)
